# Fritzing sketch ardpicprog (saved by Fritzing 0.8.3b)
circuit board: 5.33756cm x 6.9215cm
breadboards: 1

parts:
  IC1 = IC, DIP package, 18 pins [chip_label=IC]
  C1 = Electrolytic Capacitor [capacitance=1µF package="100 mil [THT, electrolytic]"]
  C2 = Ceramic Capacitor [capacitance=100nF package="100 mil [THT, multilayer]"]
  C3 = Ceramic Capacitor [capacitance=100nF package="100 mil [THT, multilayer]"]
  R1 = Resistor [tolerance=±5% resistance=10k package=THT]
  R2 = Resistor [tolerance=±5% resistance=680 package=THT]
  D1 = Rectifier Diode [part_number=1N4001 package="300 mil [THT]"]
  R4 = Resistor [tolerance=±5% resistance=1k package=THT]
  Q1 = NPN-Transistor [part_number=BC548 package="TO92 [THT]"]
  U3 = Voltage Regulator - Variable [part_number=* package="TO220 [THT]"]
  R5 = Resistor [tolerance=±5% resistance=10k package=THT]
  R6 = Resistor [tolerance=±5% resistance=4.7k package=THT]
  R7 = Resistor [tolerance=±5% resistance=220 package=THT]
  LED1 = LED - 5mm [color="Red (633nm)" package="5 mm [THT]"]
  LED2 = LED - 5mm [color="Yellow (574nm)" package="5 mm [THT]"]
  C4 = Ceramic Capacitor [capacitance=100nF voltage=16V package="100 mil [THT, multilayer]"]
  J1 = male pin header, 3 pins [form="♂ (male)"]
  S1 = Pushbutton [package="[THT]"]
  R8 = Resistor [tolerance=±5% resistance=220 package=THT]
  J2 = male pin header, 6 pins [form="♂ (male)"]
  J3 = male pin header, 2 pins [form="♂ (male)" part_number=15V]
  R3 = Trimmer Potentiometer [maximum_resistance=12kΩ part_number=* package=THT]
  Arduino1 = Arduino
  U1 = Voltage Regulator - 5V [package="TO220 [THT]"]

nets:
  N1: IC1.pin1, J1.pin3
  N2: IC1.pin4, Q1.C, R5.Pin_1, J2.pin1
  GND: IC1.pin5, IC1.pin18, C1.-, R2.Pin_1, Q1.E, LED1.cathode, LED2.cathode, C4.0, S1.Pin_3, S1.Pin_4, R8.Pin_1, J2.pin3, J3.pin1, R3.leg1, Arduino1.GND
  N3: IC1.pin10, R8.Pin_0, J2.pin6
  N4: IC1.pin12, IC1.pin16, J2.pin5, Arduino1.D4
  N5: IC1.pin13, IC1.pin17, J2.pin4, Arduino1.D7
  N6: IC1.pin14, J1.pin1
  N7: C1.+, C3.1, D1.cathode, U3.IN, U1.input_voltage
  N8: C2.0, C3.0, R1.Pin_1, R2.Pin_0, U3.ADJ, R3.wiper, U1.GND
  13V: C2.1, R1.Pin_0, R4.Pin_0, U3.OUT, R5.Pin_0, R3.leg2, U1.output_voltage
  N9: D1.anode, J3.pin2
  N10: R4.Pin_1, LED1.anode
  N11: Q1.B, R6.Pin_0
  N12: R6.Pin_1, Arduino1.A1
  N13: R7.Pin_0, LED2.anode
  N14: R7.Pin_1, Arduino1.A5
  N15: C4.1, J1.pin2, J2.pin2, Arduino1.D2
  N16: S1.Pin_1, S1.Pin_2, Arduino1.RST

notes:
  * alternative
