# Fritzing sketch denne_Svietenie_faston (saved by Fritzing 0.8.5b)
circuit board: 6cm x 3.45cm
breadboards: 1

parts:
  Q2 = Basic FET P-Channel [part_number=IRF9630 package="TO220 [THT]"]
  Q3 = Basic FET P-Channel [part_number=IRF9630 package="TO220 [THT]"]
  R1 = Resistor [tolerance=±5% resistance=10k package="1206 [SMD]"]
  Q4 = NPN-Transistor [package="SOT-23 [SMD]"]
  12V_from_battery = Faston male header [form="faston pcb 6.3x0.8"]
  12V_from_X_relay = Faston male header [form="faston pcb 6.3x0.8"]
  GND = Faston male header [form="faston pcb 6.3x0.8"]
  left_tail_and_parking_light = Faston male header [form="faston pcb 6.3x0.8"]
  license_lights = Faston male header [form="faston pcb 6.3x0.8"]
  right_tail_and_parking_light = Faston male header [form="faston pcb 6.3x0.8"]
  Q1 = Basic FET P-Channel [part_number=IRF9630 package="TO220 [THT]"]
  Q5 = Basic FET P-Channel [part_number=IRF9630 package="TO220 [THT]"]
  Q6 = Basic FET P-Channel [part_number=IRF9630 package="TO220 [THT]"]
  right_head_light = Faston male header [form="faston pcb 6.3x0.8"]
  left_head_light = Faston male header [form="faston pcb 6.3x0.8"]
  Q7 = NPN-Transistor [package="SOT-23 [SMD]"]
  R3 = Resistor [tolerance=±5% resistance=10k package="1206 [SMD]"]
  R4 = Resistor [tolerance=±5% resistance=1k package="1206 [SMD]"]
  Q8 = Basic FET P-Channel [part_number=IRF9630 package="TO220 [THT]"]
  Q9 = Basic FET P-Channel [part_number=IRF9630 package="TO220 [THT]"]
  Q10 = NPN-Transistor [package="SOT-23 [SMD]"]
  R5 = Resistor [tolerance=±5% resistance=10k package="1206 [SMD]"]
  R6 = Resistor [tolerance=±5% resistance=1k package="1206 [SMD]"]
  right_fog_light = Faston male header [form="faston pcb 6.3x0.8"]
  left_fog_light = Faston male header [form="faston pcb 6.3x0.8"]
  IC1 = Voltage Regulator [package=to-92]
  C1 = Ceramic Capacitor [capacitance=100nF package="100 mil [THT, multilayer]"]
  C2 = Ceramic Capacitor [capacitance=100nF package="100 mil [THT, multilayer]"]
  lights_switch_pin_1 = Faston male header [form="faston pcb 6.3x0.8"]
  R7 = Resistor [tolerance=±5% resistance=220 package=THT]
  R8 = Resistor [tolerance=±5% resistance=220 package=THT]
  D1 = Zener Diode [part_number=1N4732A breakdown_voltage=5.1V package="300 mil [THT]"]
  R9 = Resistor [tolerance=±5% resistance=220 package=THT]
  D2 = Zener Diode [part_number=1N4732A breakdown_voltage=5.1V package="300 mil [THT]"]
  R2 = Resistor [tolerance=±5% resistance=1k package="1206 [SMD]"]
  U1 = atmega328 [package=dip]
  Q11 = NPN-Transistor [package="SOT-23 [SMD]"]
  R10 = Resistor [tolerance=±5% resistance=10k package="1206 [SMD]"]
  R11 = Resistor [tolerance=±5% resistance=1k package="1206 [SMD]"]

nets:
  N1: Q2.gate, Q3.gate, R1.Pin_1, Q4.1, Q1.gate
  N2: Q2.drain, Q3.drain, R1.Pin_0, 12V_from_battery.pin1, Q1.drain, Q5.drain, Q6.drain, R3.Pin_0, Q8.drain, Q9.drain, R5.Pin_0, IC1.IN, C1.1, R10.Pin_0
  N3: Q2.source, license_lights.pin1
  N4: Q3.source, right_tail_and_parking_light.pin1
  GND: Q4.2, GND.pin1, Q7.2, Q10.2, IC1.GND, C1.0, C2.0, D1.anode, D2.anode, U1.GND, Q11.2
  N5: Q4.0, R2.Pin_1
  N6: 12V_from_X_relay.pin1, R9.Pin_1, R2.Pin_0
  N7: left_tail_and_parking_light.pin1, Q1.source
  N8: Q5.gate, Q6.gate, Q7.1, R3.Pin_1
  N9: Q5.source, left_head_light.pin1
  N10: Q6.source, right_head_light.pin1
  N11: Q7.0, R4.Pin_1
  N12: R4.Pin_0, U1.D11_(PWM)
  N13: Q8.gate, Q11.1, R10.Pin_1
  N14: Q8.source, right_fog_light.pin1
  N15: Q9.gate, Q10.1, R5.Pin_1
  N16: Q9.source, left_fog_light.pin1
  N17: Q10.0, R6.Pin_1
  N18: R6.Pin_0, U1.D10_(PWM)
  N19: IC1.OUT, C2.1, R7.Pin_0, U1.VCC, U1.AREF
  N20: lights_switch_pin_1.pin1, R8.Pin_1
  N21: R7.Pin_1, U1.RESET
  N22: R8.Pin_0, D1.cathode, U1.A1
  N23: R9.Pin_0, D2.cathode, U1.A0
  N24: U1.D9_(PWM), R11.Pin_0
  N25: Q11.0, R11.Pin_1

notes:
  GND
  SWITCH
  BAT
  out1
  out2
  out3
  box: gme.sk U-KM31
  ( 622-158)

custom parts:
  Faston male header: Faston male header 6.3x0,8mm PCB
