# Fritzing sketch denne_Svietenie_rele_D+D_faston (saved by Fritzing 0.8.0b)
breadboards: 1

parts:
  D1 = P1000K [part_number=P1000K]
  D2 = P1000K [part_number=P1000K]
  J1 = Faston male header [form="faston pcb 6.3x0.8"]
  J2 = Faston male header [form="faston pcb 6.3x0.8"]
  J3 = Faston male header [form="faston pcb 6.3x0.8"]
  J4 = Faston male header [form="faston pcb 6.3x0.8"]
  J5 = Faston male header [form="faston pcb 6.3x0.8"]
  J6 = Faston male header [form="faston pcb 6.3x0.8"]
  J90 = CAR RELAY [part_number=NVF4-2 package=THT]
  J7 = Faston male header [form="faston pcb 6.3x0.8"]
  low_beams = Faston male header [form="faston pcb 6.3x0.8"]
  J9 = Faston male header [form="faston pcb 6.3x0.8"]
  D3 = P1000K [part_number=P1000K]
  J336 = CAR RELAY [part_number=NVF4-2 package=THT]
  R1 = Resistor [tolerance=±5% resistance=0 package=THT]
  R2 = Resistor [tolerance=±5% resistance=0 package=THT]

nets:
  N1: D1.cathode, J5.pin1
  N2: D1.anode, D2.anode, J90.30, D3.anode
  N3: D2.cathode, J3.pin1
  N4: J1.pin1, J90.86
  N5: J2.pin1, J90.87
  N6: J4.pin1, D3.cathode
  N7: J6.pin1, J90.85, J336.85
  N8: J7.pin1, J336.86
  N9: low_beams.pin1, R2.Pin_0
  N10: J9.pin1, J336.30
  N11: J336.87, R1.Pin_1
  N12: R1.Pin_0, R2.Pin_1

notes:
  R1+R2
  Pz
  Pr1,Pr2
  1.5
  22.2264115374
  12.7250447733
  1.2
  25.8545544256
  11.8417806529
  1
  28.7903299655
  10.9886755594
  0.65
  35.2832253177
  8.75347193
  0.68
  34.6446280992
  8.9917355372
  0.47
  39.5136205109
  7.0883212367
  0.33
  43.3530594657
  5.4604998564
  0.22
  46.7764332474
  3.9277921047
  0.1
  50.9948096886
  1.946366782

custom parts:
  P1000K: A standard rectifier diode 10A
  Faston male header: Faston male header 6.3x0,8mm PCB
