# Fritzing sketch denne_Svietenie_rele_D (saved by Fritzing 0.7.12b)
breadboards: 1

parts:
  J1 = screw terminal, 6 pins
  RELAY1 = CAR RELAY [part_number=NVF4-2 package=THT]
  D1 = P1000K [part_number=P1000K]
  D3 = P1000K [part_number=P1000K]
  D2 = P1000K [part_number=P1000K]

nets:
  N1: J1.pin1, RELAY1.85
  N2: J1.pin2, RELAY1.87
  N3: J1.pin3, RELAY1.86
  N4: J1.pin4, D2.cathode
  N5: J1.pin5, D3.cathode
  N6: J1.pin6, D1.cathode
  N7: RELAY1.30, D1.anode, D3.anode, D2.anode

custom parts:
  P1000K: A standard rectifier diode 10A
