# Fritzing sketch denne_Svietenie_rele_D_faston (saved by Fritzing 0.8.0b)
breadboards: 1

parts:
  D1 = P1000K [part_number=P1000K]
  D3 = P1000K [part_number=P1000K]
  D2 = P1000K [part_number=P1000K]
  J1 = Faston male header [form="faston pcb 6.3x0.8"]
  J2 = Faston male header [form="faston pcb 6.3x0.8"]
  J3 = Faston male header [form="faston pcb 6.3x0.8"]
  J4 = Faston male header [form="faston pcb 6.3x0.8"]
  J5 = Faston male header [form="faston pcb 6.3x0.8"]
  J6 = Faston male header [form="faston pcb 6.3x0.8"]
  RELAY1 = CAR RELAY [part_number=NVF4-2 package=THT]

nets:
  N1: D1.cathode, J5.pin1
  N2: D1.anode, D3.anode, D2.anode, RELAY1.30
  N3: D3.cathode, J4.pin1
  N4: D2.cathode, J3.pin1
  N5: J1.pin1, RELAY1.85
  N6: J2.pin1, RELAY1.87
  N7: J6.pin1, RELAY1.86

notes:
  box: gme.sk U-KM31
  ( 622-158)

custom parts:
  P1000K: A standard rectifier diode 10A
  Faston male header: Faston male header 6.3x0,8mm PCB
