# Fritzing sketch denne_Svietenie_rele_D_stad_up (saved by Fritzing 0.8.0b)
breadboards: 1

parts:
  J1 = screw terminal, 6 pins
  RELAY1 = CAR RELAY [part_number=NVF4-2 package=THT]
  D6 = P1000K [part_number=P1000K]
  D4 = P1000K [part_number=P1000K]
  D5 = P1000K [part_number=P1000K]

nets:
  N1: J1.pin1, RELAY1.85
  N2: J1.pin2, RELAY1.87
  N3: J1.pin3, RELAY1.86
  N4: J1.pin4, D4.cathode
  N5: J1.pin5, D5.cathode
  N6: J1.pin6, D6.cathode
  N7: RELAY1.30, D6.anode, D4.anode, D5.anode

custom parts:
  P1000K: A standard rectifier diode 10A
