# Fritzing sketch denne_Svietenie_rele_faston (saved by Fritzing 0.8.0b)
breadboards: 1

parts:
  OMRON1 = OMRON PCB Power Relay – G5LE [part_number="G5LE-1 \n" package=THT]
  OMRON2 = OMRON PCB Power Relay – G5LE [part_number="G5LE-1 \n" package=THT]
  OMRON3 = OMRON PCB Power Relay – G5LE [part_number="G5LE-1 \n" package=THT]
  J1 = Faston male header [form="faston pcb 6.3x0.8"]
  J2 = Faston male header [form="faston pcb 6.3x0.8"]
  J3 = Faston male header [form="faston pcb 6.3x0.8"]
  J4 = Faston male header [form="faston pcb 6.3x0.8"]
  J5 = Faston male header [form="faston pcb 6.3x0.8"]
  J6 = Faston male header [form="faston pcb 6.3x0.8"]

nets:
  N1: OMRON1.COIL1, OMRON2.COIL1, OMRON3.COIL1, J6.pin1
  N2: OMRON1.C, OMRON2.C, OMRON3.C, J3.pin1
  N3: OMRON1.COIL2, OMRON2.COIL2, OMRON3.COIL2, J2.pin1
  N4: OMRON1.B, J1.pin1
  N5: OMRON2.B, J4.pin1
  N6: OMRON3.B, J5.pin1

notes:
  box: gme.sk U-KM31
  ( 622-158)

custom parts:
  Faston male header: Faston male header 6.3x0,8mm PCB
