# Fritzing sketch microSD_adapter_for_rPi (saved by Fritzing 0.8.3b)
circuit board: 2.42494cm x 1.7439cm
breadboards: 1

parts:
  U1 = microSD Socket [package="112-TXAR-R01 [SMD]"]
  SD1 = SD Card [part_number=sdcard]

nets:
  N1: U1.CS, SD1.CS
  N2: U1.DI, SD1.DI
  VCC: U1.VCC, SD1.VCC
  N3: U1.SCK, SD1.SCK
  GND: U1.GND, U1.SHIELD, SD1.GND, SD1.GND1
  N4: U1.DO, SD1.DO

custom parts:
  microSD Socket: 112-TXAR-R01 microSD socket.
