# Fritzing sketch emulator_pic_BT_THT_parts_v3 (saved by Fritzing 0.8.5b)
circuit board: 6.82433cm x 4.34673cm
breadboards: 1

parts:
  IC1 = IC, DIP package, 8 pins [chip_label="PIC 12F629"]
  IC2 = IC, DIP package, 8 pins [chip_label=NE5532I]
  R1 = Resistor [tolerance=±5% resistance=3.3k package=THT]
  R2 = Resistor [tolerance=±5% resistance=3.3k package=THT]
  R3 = Resistor [tolerance=±5% resistance=3.3k package=THT]
  R5 = Resistor [tolerance=±5% resistance=10k package=THT]
  R6 = Resistor [tolerance=±5% resistance=10k package=THT]
  R7 = Resistor [tolerance=±5% resistance=100k package=THT]
  R8 = Resistor [tolerance=±5% resistance=100k package=THT]
  R9 = Resistor [tolerance=±5% resistance=330k package=THT]
  R10 = Resistor [tolerance=±5% resistance=330k package=THT]
  R11 = Resistor [tolerance=±5% resistance=10k package=THT]
  R12 = Resistor [tolerance=±5% resistance=10k package=THT]
  R13 = Resistor [tolerance=±5% resistance=7.5M package=THT]
  R14 = Resistor [tolerance=±5% resistance=7.5M package=THT]
  C4 = Ceramic Capacitor [capacitance=100nF voltage=20V package="100 mil [THT, multilayer]"]
  C6 = Electrolytic Capacitor [capacitance=10µF voltage=50V package="100 mil [THT, electrolytic]"]
  C7 = Electrolytic Capacitor [capacitance=47µF voltage=50V package="100 mil [THT, electrolytic]"]
  C8 = Electrolytic Capacitor [capacitance=47µF voltage=50V package="100 mil [THT, electrolytic]"]
  R21 = Resistor [tolerance=±5% resistance=10k package=THT]
  J5 = screw terminal, 6 pins
  J4 = screw terminal, 3 pins
  IC10 = IC, DIP package, 14 pins [chip_label=4066]
  R60 = Resistor [tolerance=±5% resistance=10k package=THT]
  C24 = Ceramic Capacitor [capacitance=15pF package="100 mil [THT, multilayer]"]
  L6 = Inductor [inductance=15n package="400 mil [THT]"]
  C5 = Electrolytic Capacitor [capacitance=10µF voltage=50V package="100 mil [THT, electrolytic]"]
  J6 = female pin header, 2 pins [form="♀ (female)"]
  U8 = Voltage Regulator [package=to-92]
  IC11 = IC, DIP package, 8 pins [chip_label=Attiny85]
  C26 = Electrolytic Capacitor [capacitance=2.2µF voltage=20V package="100 mil [THT, electrolytic]"]
  R61 = Resistor [tolerance=±5% resistance=10k package=THT]
  LED2 = LED - 3mm [color="Green (570nm)" package="3 mm [THT]"]
  LED1 = LED - 3mm [color="Red (660nm)" package="3 mm [THT]"]
  R62 = Resistor [tolerance=±5% resistance=10k package=THT]
  C23 = Ceramic Capacitor [capacitance=100nF voltage=20V package="100 mil [THT, multilayer]"]
  R19 = Resistor [tolerance=±5% resistance=1k package=THT]
  C9 = Electrolytic Capacitor [capacitance=2.2µF voltage=20V package="100 mil [THT, electrolytic]"]
  C3 = Ceramic Capacitor [capacitance=100nF voltage=20V package="100 mil [THT, multilayer]"]
  CM-15113_(BTM-68D)3 = Bluetooth Audio Module [part_number=BTM-68D package=SMD]
  U7 = Voltage Regulator [part_number=HT7533-1 package=to-92]

nets:
  5V: IC1.pin1, R21.Pin_0, IC10.pin14, U8.OUT, IC11.pin8, C3.1, U7.IN
  N1: IC1.pin2, R1.Pin_1
  N2: IC1.pin3, R2.Pin_1
  PullUp: IC1.pin4, R21.Pin_1, IC10.pin2, IC11.pin1
  N3: IC1.pin5, R3.Pin_1
  N4: IC1.pin6, R19.Pin_0
  GND: IC1.pin8, IC2.pin4, R5.Pin_0, R6.Pin_0, R12.Pin_0, C4.0, J5.pin3, J4.pin2, IC10.pin7, U8.GND, IC11.pin4, C23.0, C9.-, C3.0, CM-15113_(BTM-68D)3.GND, CM-15113_(BTM-68D)3.AGND, U7.GND
  N5: IC2.pin1, R14.Pin_0, C7.-
  N6: IC2.pin2, R9.Pin_1, R14.Pin_1
  N7: IC2.pin3, R8.Pin_1, C5.+
  N8: IC2.pin5, R7.Pin_1, C6.+
  N9: IC2.pin6, R10.Pin_1, R13.Pin_0
  N10: IC2.pin7, R13.Pin_1, C8.-
  12V: IC2.pin8, R11.Pin_1, J5.pin1, C26.+
  CLK: R1.Pin_0, J5.pin4
  datain: R2.Pin_0, J5.pin5
  dataOut: R3.Pin_0, J5.pin6
  rightIn: R5.Pin_1, C5.-, CM-15113_(BTM-68D)3.L+
  LeftIn: R6.Pin_1, C6.-, CM-15113_(BTM-68D)3.R+
  N11: R7.Pin_0, R8.Pin_0, R9.Pin_0, R10.Pin_0, R11.Pin_0, R12.Pin_1, C26.-, C9.+
  switchON: C4.1, J5.pin2, U8.IN
  RightOut: C7.+, J4.pin1
  LeftOut: C8.+, J4.pin3
  N12: IC10.pin1, CM-15113_(BTM-68D)3.Vreg
  N13: IC10.pin3, IC10.pin9, IC10.pin10, R60.Pin_0
  N14: IC10.pin4, CM-15113_(BTM-68D)3.PIO[13]
  N15: IC10.pin5, IC11.pin2
  N16: IC10.pin6, IC11.pin5
  N17: IC10.pin8, CM-15113_(BTM-68D)3.PIO[14]
  N18: IC10.pin11, CM-15113_(BTM-68D)3.PIO[5]
  N19: IC10.pin12, IC11.pin7
  N20: IC10.pin13, IC11.pin3
  N21: R60.Pin_1, CM-15113_(BTM-68D)3.1V8
  N22: C24.0, L6.pin_1, CM-15113_(BTM-68D)3.MIC_BIAS
  N23: C24.1, J6.pin1, CM-15113_(BTM-68D)3.MIC+
  N24: L6.pin_0, J6.pin2
  9600: IC11.pin6, R19.Pin_1
  N25: R61.Pin_0, CM-15113_(BTM-68D)3.RST#
  3.3: R61.Pin_1, R62.Pin_1, C23.1, CM-15113_(BTM-68D)3.BAT_IN, U7.OUT
  N26: LED2.cathode, CM-15113_(BTM-68D)3.LED[0]
  N27: LED2.anode, LED1.anode, R62.Pin_0
  N28: LED1.cathode, CM-15113_(BTM-68D)3.LED[1]

notes:
  RS232
  phone_controled_by_arduino_over_BT.ino
  POWERON->PB4
  PREV/FW -> PB2
  NEXT/RW -> PB0
  PLAY -> PB3

custom parts:
  Bluetooth Audio Module: BTM-68D is the latest generation of bluetooth Module. It provides highest level of integration with integrated 2.4GHz radio, DSP, battery charger, stereo codec, and antenna ready. Mono and stereo audio applications. BTM-68D is also ready to support the latest Bluetooth 2.1 standard and support for secure Simple pairing.
