# Fritzing sketch emulator_pic_HTC (saved by Fritzing 0.9.0b)
circuit board: 6.27705cm x 4.58988cm
breadboards: 1

parts:
  IC1 = IC, DIP package, 8 pins [chip_label="PIC 12F629"]
  IC2 = IC, DIP package, 8 pins [chip_label=NE5532I]
  U1 = Voltage Regulator - 5V [package="TO220 [THT]"]
  R1 = Resistor [tolerance=±5% resistance=3.3k package=THT]
  R2 = Resistor [tolerance=±5% resistance=3.3k package=THT]
  R3 = Resistor [tolerance=±5% resistance=3.3k package=THT]
  R4 = Resistor [tolerance=±5% resistance=10 package=THT]
  R5 = Resistor [tolerance=±5% resistance=10k package=THT]
  R6 = Resistor [tolerance=±5% resistance=10k package=THT]
  R7 = Resistor [tolerance=±5% resistance=100k package=THT]
  R8 = Resistor [tolerance=±5% resistance=100k package=THT]
  R9 = Resistor [tolerance=±5% resistance=330k package=THT]
  R10 = Resistor [tolerance=±5% resistance=330k package=THT]
  R11 = Resistor [tolerance=±5% resistance=10k package=THT]
  R12 = Resistor [tolerance=±5% resistance=10k package=THT]
  R13 = Resistor [tolerance=±5% resistance=7.5M package=THT]
  R14 = Resistor [tolerance=±5% resistance=7.5M package=THT]
  R15 = Resistor [tolerance=±5% resistance=12k package=THT]
  R16 = Resistor [tolerance=±5% resistance=1k package=THT]
  R17 = Resistor [tolerance=±5% resistance=12k package=THT]
  R18 = Resistor [tolerance=±5% resistance=1k package=THT]
  L1 = Inductor [inductance=330µ package="400 mil [THT]"]
  D1 = Rectifier Diode [part_number=1N4007 package="300 mil [THT]"]
  C1 = Electrolytic Capacitor [capacitance=0.1mF voltage=20V package="100 mil [THT, electrolytic]"]
  C2 = Electrolytic Capacitor [capacitance=47µF voltage=20V package="100 mil [THT, electrolytic]"]
  C3 = Ceramic Capacitor [capacitance=100nF voltage=20V package="100 mil [THT, multilayer]"]
  C4 = Ceramic Capacitor [capacitance=100nF voltage=20V package="100 mil [THT, multilayer]"]
  C6 = Electrolytic Capacitor [capacitance=10µF voltage=50V package="100 mil [THT, electrolytic]"]
  C7 = Electrolytic Capacitor [capacitance=47µF voltage=50V package="100 mil [THT, electrolytic]"]
  C8 = Electrolytic Capacitor [capacitance=47µF voltage=50V package="100 mil [THT, electrolytic]"]
  C9 = Electrolytic Capacitor [capacitance=2.2µF voltage=20V package="100 mil [THT, electrolytic]"]
  C5 = Electrolytic Capacitor [capacitance=10µF voltage=50V package="100 mil [THT, electrolytic]"]
  R19 = Resistor [tolerance=±5% resistance=1k package=THT]
  R20 = Resistor [tolerance=±5% resistance=1k package=THT]
  J2 = male pin header, 3 pins [form="♂ (male)" part_number=rs232]
  R21 = Resistor [tolerance=±5% resistance=10k package=THT]
  J5 = screw terminal, 6 pins
  J4 = screw terminal, 3 pins
  J3 = screw terminal, 4 pins
  R57 = Resistor [tolerance=±5% resistance=1.2k package=THT]
  R56 = Resistor [tolerance=±5% resistance=560 package=THT]
  IC7 = IC, DIP package, 8 pins [chip_label=Attiny85]
  R55 = Resistor [tolerance=±5% resistance=220 package=THT]
  Q7 = NPN-Transistor [package="TO92 [THT]"]
  Q6 = NPN-Transistor [package="TO92 [THT]"]
  Q5 = NPN-Transistor [package="TO92 [THT]"]
  Q8 = NPN-Transistor [package="TO92 [THT]"]
  Q9 = PNP-Transistor [package="TO92 [THT]"]
  R53 = Resistor [tolerance=±5% resistance=1.2k package=THT]
  R54 = Resistor [tolerance=±5% resistance=1.2k package=THT]
  part = Resistor [tolerance=±5% resistance=220 package=THT]  # not connected

nets:
  N1: IC1.pin1, U1.output_voltage, C3.1, R21.Pin_0, IC7.pin8
  N2: IC1.pin2, R19.Pin_0
  N3: IC1.pin3, R20.Pin_0
  N4: IC1.pin4, R21.Pin_1
  N5: IC1.pin5, R3.Pin_1
  N6: IC1.pin6, R2.Pin_1
  N7: IC1.pin7, R1.Pin_1
  GND: IC1.pin8, U1.GND, R4.Pin_1, R16.Pin_1, C1.-, C2.-, C3.0, C4.0, J2.pin2, J5.pin4, IC7.pin4, Q7.E, Q6.E, Q5.E, Q8.E
  N8: IC2.pin1, R14.Pin_0, C7.-
  N9: IC2.pin2, R9.Pin_1, R14.Pin_1
  N10: IC2.pin3, R8.Pin_1, C5.+
  N11: IC2.pin4, R4.Pin_0, R5.Pin_0, R6.Pin_0, R12.Pin_0, C9.-, J4.pin2, J3.pin2
  N12: IC2.pin5, R7.Pin_1, C6.+
  N13: IC2.pin6, R10.Pin_1, R13.Pin_0
  N14: IC2.pin7, R13.Pin_1, C8.-
  N15: IC2.pin8, U1.input_voltage, R11.Pin_1, L1.pin_0, C2.+, C4.1
  N16: R1.Pin_0, J5.pin3
  N17: R2.Pin_0, J5.pin2
  N18: R3.Pin_0, J5.pin1
  N19: R5.Pin_1, C5.-, J3.pin1
  N20: R6.Pin_1, C6.-, J3.pin3
  N21: R7.Pin_0, R8.Pin_0, R9.Pin_0, R10.Pin_0, R11.Pin_0, R12.Pin_1, C9.+
  N22: R15.Pin_0, R16.Pin_0, Q8.B
  N23: R15.Pin_1, J5.pin5
  N24: R17.Pin_0, R18.Pin_0, Q9.B
  N25: R17.Pin_1, Q8.C
  N26: R18.Pin_1, D1.cathode, Q9.E
  N27: L1.pin_1, C1.+, Q9.C
  N28: D1.anode, J5.pin6
  N29: C7.+, J4.pin3
  N30: C8.+, J4.pin1
  N31: R19.Pin_1, J2.pin3, IC7.pin3
  N32: R20.Pin_1, J2.pin1
  PhoneRemoteControl: J3.pin4, R56.Pin_1, R55.Pin_1, Q5.C
  N33: R57.Pin_0, Q7.B
  N34: R57.Pin_1, IC7.pin2
  N35: R56.Pin_0, Q7.C
  N36: IC7.pin6, R54.Pin_1
  N37: IC7.pin7, R53.Pin_1
  N38: R55.Pin_0, Q6.C
  N39: Q6.B, R53.Pin_0
  N40: Q5.B, R54.Pin_0

notes:
  NE5532
  12F529
  PIC
  19200
  9600
  GND
  RS232
  previous
  next
  play/pause
