# Fritzing sketch emulator_smd_Bluetooth (saved by Fritzing 0.8.3b)
circuit board: 6.83312cm x 2.68224cm
breadboards: 1

parts:
  rs232 = longpad pin header, 3 pins [form="long pad"]
  R34 = Resistor [tolerance=±5% resistance=10k package="1206 [SMD]"]
  R30 = Resistor [tolerance=±5% resistance=330k package="1206 [SMD]"]
  R33 = Resistor [tolerance=±5% resistance=100k package="1206 [SMD]"]
  R28 = Resistor [tolerance=±5% resistance=10k package="1206 [SMD]"]
  R32 = Resistor [tolerance=±5% resistance=100k package="1206 [SMD]"]
  R31 = Resistor [tolerance=±5% resistance=330k package="1206 [SMD]"]
  R29 = Resistor [tolerance=±5% resistance=10k package="1206 [SMD]"]
  R35 = Resistor [tolerance=±5% resistance=10k package="1206 [SMD]"]
  R26 = Resistor [tolerance=±5% resistance=7.5M package="1206 [SMD]"]
  R27 = Resistor [tolerance=±5% resistance=7.5M package="1206 [SMD]"]
  IC4 = SO08 [chip_label=NE5532I package=SO]
  C16 = Electrolytic Capacitor [capacitance=47µF voltage=50V package="0605 [SMD, electrolytic]"]
  C18 = Electrolytic Capacitor [capacitance=10µF voltage=50V package="0605 [SMD, electrolytic]"]
  C15 = Tantalum Capacitor [capacitance=2.2µF voltage=20V package="A 3216 [SMD, tantalum]"]
  radio = longpad pin header, 9 pins [form="long pad"]
  ICSP = longpad pin header, 5 pins [form="long pad"]
  IC3 = SO08 [chip_label="PIC 12F629" package=SO]
  R41* = Resistor [tolerance=±5% resistance=1k package="1206 [SMD]"]
  R48** = Resistor [tolerance=±5% resistance=3.3k package="1206 [SMD]"]
  R48* = Resistor [tolerance=±5% resistance=3.3k package="1206 [SMD]"]
  R41** = Resistor [tolerance=±5% resistance=1k package="1206 [SMD]"]
  R46 = Resistor [tolerance=±5% resistance=3.3k package="1206 [SMD]"]
  R47* = Resistor [tolerance=±5% resistance=3.3k package="1206 [SMD]"]
  R40* = Resistor [tolerance=±5% resistance=1k package="1206 [SMD]"]
  R47** = Resistor [tolerance=±5% resistance=3.3k package="1206 [SMD]"]
  R47 = Resistor [tolerance=±5% resistance=10 package="1206 [SMD]"]
  C17 = Electrolytic Capacitor [capacitance=47µF voltage=50V package="0605 [SMD, electrolytic]"]
  C12 = Ceramic Capacitor [capacitance=100nF voltage=20V package="1206 [SMD, multilayer]"]
  L3 = Inductor [package="1010 [SMD]"]
  C11 = Electrolytic Capacitor [capacitance=0.1mF voltage=25V package="0605 [SMD, electrolytic]"]
  R44 = Resistor [tolerance=±5% resistance=1.5k package="1206 [SMD]"]
  R45 = Resistor [tolerance=±5% resistance=1k package="1206 [SMD]"]
  IC5 = SO08 [chip_label=IRF7309 package=SO]
  R43 = Resistor [tolerance=±5% resistance=1M package="1206 [SMD]"]
  Q1 = PNP-Transistor [package="SOT-23 [SMD]"]
  C19 = Tantalum Capacitor [capacitance=2.2µF voltage=20V package="A 3216 [SMD, tantalum]"]
  C10 = Electrolytic Capacitor [capacitance=47µF voltage=25V package="0605 [SMD, electrolytic]"]
  C13 = Ceramic Capacitor [capacitance=100nF voltage=20V package="1206 [SMD, multilayer]"]
  R42 = Resistor [tolerance=±5% resistance=10k package="1206 [SMD]"]
  R40** = Resistor [tolerance=±5% resistance=1k package="1206 [SMD]"]
  C14 = Electrolytic Capacitor [capacitance=10µF voltage=50V package="0605 [SMD, electrolytic]"]
  U5 = Voltage Regulator [part_number=3.3V package=sot223]
  C20 = Ceramic Capacitor [capacitance=100nF voltage=20V package="1206 [SMD, multilayer]"]
  U6 = Voltage Regulator [package=sot223]
  IC7 = SOIC-14 [chip_label=4066 package=SO]
  IC6 = SO08 [chip_label=Attiny85 package=SO]
  R51 = Resistor [tolerance=±5% resistance=10k package="1206 [SMD]"]
  R50 = Resistor [tolerance=±5% resistance=10k package="1206 [SMD]"]
  R48 = Resistor [tolerance=±5% resistance=10k package="1206 [SMD]"]
  R49 = Resistor [tolerance=±5% resistance=10k package="1206 [SMD]"]
  CM-15113_(BTM-68D)1 = Bluetooth Audio Module [part_number=BTM-68D package=SMD]
  C21 = Ceramic Capacitor [capacitance=15pF package="1206 [SMD, multilayer]"]
  L4 = Inductor [inductance=15n package="1206 [SMD]"]
  Pad1 = Pad [width=3.52681817426603 height=2.6423719269329 connect=east]
  Pad2 = Pad [width=3.6938455578212 height=2.75653911224393 connect=east]

nets:
  19200: rs232.pin1, R40*.Pin_1, R40**.Pin_1
  GND: rs232.pin2, radio.pin4, ICSP.pin3, IC3.8, R47.Pin_0, C12.0, C11.-, IC5.1, R43.Pin_1, C19.-, C10.-, C13.0, U5.ADJ, C20.0, U6.ADJ, IC7.7, IC6.4, CM-15113_(BTM-68D)1.GND
  9600: rs232.pin3, R41*.Pin_1, R41**.Pin_1, IC6.3
  N1: R34.Pin_0, R30.Pin_0, R33.Pin_0, R28.Pin_1, R32.Pin_0, R31.Pin_0, R29.Pin_0, R35.Pin_0, C15.+
  LeftIn: R34.Pin_1, C18.-, CM-15113_(BTM-68D)1.L+
  N2: R30.Pin_1, R27.Pin_0, IC4.6
  N3: R33.Pin_1, IC4.5, C18.+
  audioGND: R28.Pin_0, IC4.4, C15.-, radio.pin8, R47.Pin_1, CM-15113_(BTM-68D)1.AGND
  N4: R32.Pin_1, IC4.3, C14.+
  N5: R31.Pin_1, R26.Pin_1, IC4.2
  12Vswitched: R29.Pin_1, IC4.8, C12.1, L3.pin_0, C10.+, U6.IN
  rightIn: R35.Pin_1, C14.-, CM-15113_(BTM-68D)1.R+
  N6: R26.Pin_0, IC4.1, C17.-
  N7: R27.Pin_1, IC4.7, C16.-
  leftOut: C16.+, radio.pin9
  dataIn: radio.pin1, R47*.Pin_0, R47**.Pin_0
  clock: radio.pin2, R48**.Pin_0, R48*.Pin_0
  dataOut: radio.pin3, R46.Pin_0
  switch: radio.pin5, Q1.0
  12Vbat: radio.pin6, R45.Pin_0, IC5.3
  rightOut: radio.pin7, C17.+
  N8: ICSP.pin1, IC3.4, R42.Pin_1
  5V: ICSP.pin2, IC3.1, C13.1, R42.Pin_0, U5.IN, U6.OUT, IC7.14, IC6.8, R51.Pin_0, R50.Pin_1, R48.Pin_1
  N9: ICSP.pin4, IC3.7, R48*.Pin_1, R40**.Pin_0
  N10: ICSP.pin5, IC3.6, R41**.Pin_0, R47*.Pin_1
  N11: IC3.2, R41*.Pin_0, R48**.Pin_1
  N12: IC3.3, R40*.Pin_0, R47**.Pin_1
  N13: IC3.5, R46.Pin_1
  N14: L3.pin_1, C11.+, IC5.5, IC5.6
  N15: R44.Pin_0, R45.Pin_1, IC5.4
  N16: R44.Pin_1, IC5.7, IC5.8
  N17: IC5.2, R43.Pin_0, Q1.1, C19.+
  3.3: U5.OUT, C20.1, CM-15113_(BTM-68D)1.BAT_IN
  N18: IC7.1, CM-15113_(BTM-68D)1.PIO[13]
  N19: IC7.2, IC7.3, IC7.10, R49.Pin_0
  N20: IC7.4, CM-15113_(BTM-68D)1.PIO[14]
  N21: IC7.5, IC6.2
  N22: IC7.6, IC6.7
  N23: IC7.8, CM-15113_(BTM-68D)1.Vreg
  N24: IC7.9, R48.Pin_0
  N25: IC7.11, CM-15113_(BTM-68D)1.PIO[5]
  N26: IC7.12, IC6.6
  N27: IC7.13, IC6.5
  N28: IC6.1, R50.Pin_0
  N29: R51.Pin_1, CM-15113_(BTM-68D)1.RST#
  N30: R49.Pin_1, CM-15113_(BTM-68D)1.1V8
  N31: CM-15113_(BTM-68D)1.MIC_BIAS, C21.0, L4.pin_1
  N32: CM-15113_(BTM-68D)1.MIC+, C21.1, Pad1.pad
  N33: L4.pin_0, Pad2.pad

notes:
  9600
  GND
  19200
  dataIn
  clock
  dataout
  gnd
  12V
  switch
  Rout
  Agnd
  Lout
  phone_controled_by_arduino_over_BT.ino

custom parts:
  Bluetooth Audio Module: BTM-68D is the latest generation of bluetooth Module. It provides highest level of integration with integrated 2.4GHz radio, DSP, battery charger, stereo codec, and antenna ready. Mono and stereo audio applications. BTM-68D is also ready to support the latest Bluetooth 2.1 standard and support for secure Simple pairing.
